// Logisim project OneBit.circ as structural Verilog: 3 circuits, main circuit main
module main (
  input  in_1
);
endmodule

module Register (
  input  In_Bus,
  input  Clock,
  input  Read,
  input  Write
);

  wire and_1_out, and_2_out, and_3_out, nand_1_out, nand_2_out, nand_3_out, nand_4_out, not_1_out, or_1_out;

  or or_1 (or_1_out, In_Bus, and_1_out);
  and and_1 (and_1_out, nand_4_out, Write);
  and and_2 (and_2_out, Clock, Read);
  and and_3 (and_3_out, Read, or_1_out);
  not not_1 (not_1_out, and_3_out);
  nand nand_1 (nand_1_out, not_1_out, and_2_out);
  nand nand_2 (nand_2_out, and_2_out, and_3_out);
  nand nand_3 (nand_3_out, nand_1_out, nand_4_out);
  nand nand_4 (nand_4_out, nand_3_out, nand_2_out);

  // Notes on the sheet:
  //   Data
endmodule

module Test2 (
  input  in_1,
  input  in_2
);

  wire pull_resistor_1_node;

  Pull_Resistor #(.pull(1)) pull_resistor_1 (.node(pull_resistor_1_node));
  or or_1 (pull_resistor_1_node, in_1, in_2);
endmodule
